# Fritzing sketch fifider (saved by Fritzing 0.9.2b)
circuit board: 7.98195cm x 6.78877cm
breadboards: 1

parts:
  U3 = 74HC595 [part_number=IC1 package="DIP16 [THT]"]
  U4 = 74HC595 [part_number=IC2 package="DIP16 [THT]"]
  LED3 = smd LED [color="Red (633nm)" package="1206 [SMD]"]
  LED2 = smd LED [color="Red (633nm)" package="1206 [SMD]"]
  IC1 = IC, DIP package, 16 pins [chip_label=IC part_number=NPN]
  C1 = Ceramic Capacitor [capacitance=100nF package="100 mil [THT, multilayer]"]
  J1 = male pin header, 7 pins [form="♂ (male)"]
  LED1 = smd LED [color="Red (633nm)" package="1206 [SMD]"]
  R7 = Resistor [tolerance=±5% resistance=10k package=THT]
  R8 = Resistor [tolerance=±5% resistance=10k package=THT]
  R9 = Resistor [tolerance=±5% resistance=10k package=THT]
  R10 = Resistor [tolerance=±5% resistance=10k package=THT]
  R11 = Resistor [tolerance=±5% resistance=10k package=THT]
  J2 = male pin header, 12 pins [form="♂ (male)"]
  J3 = female pin header, 2 pins [form="♀ (female)"]
  R3 = Resistor [tolerance=±5% resistance=10k package=THT]
  R4 = Resistor [tolerance=±5% resistance=10k package=THT]
  R5 = Resistor [tolerance=±5% resistance=10k package=THT]
  R6 = Resistor [tolerance=±5% resistance=10k package=THT]
  J5 = female pin header, 2 pins [form="♀ (female)"]
  J4 = female pin header, 2 pins [form="♀ (female)"]
  J6 = female pin header, 2 pins [form="♀ (female)"]

nets:
  N1: U3.Q1, R8.Pin_1
  N2: U3.Q2, R9.Pin_1
  N3: U3.Q3, R10.Pin_1
  N4: U3.Q4, R11.Pin_1
  GND: U3.GND, U3.OE, U4.GND, U4.OE, IC1.pin6, IC1.pin7, IC1.pin8, C1.1, J3.pin2, J5.pin2, J4.pin2, J6.pin2
  5V: U3.MR, U3.VCC, U4.MR, U4.VCC, R3.Pin_0, R4.Pin_0, R5.Pin_0, R6.Pin_0
  N5: U3.SH_CP, U4.SH_CP, J1.pin3
  N6: U3.ST_CP, U4.ST_CP, C1.0, J1.pin2
  N7: U3.DS, U4.Q7'
  N8: U3.Q0, R7.Pin_1
  N9: U4.Q1, LED2.cathode, J2.pin11
  N10: U4.Q2, LED3.cathode, J2.pin10
  N11: U4.Q3, J2.pin9
  N12: U4.Q4, J2.pin8
  N13: U4.Q5, J2.pin7
  N14: U4.Q6, J2.pin6
  N15: U4.DS, J1.pin1
  N16: U4.Q0, LED1.cathode, J2.pin12
  N17: LED3.anode, LED2.anode, IC1.pin12, LED1.anode
  N18: IC1.pin1, R7.Pin_0
  N19: IC1.pin2, R8.Pin_0
  N20: IC1.pin3, R9.Pin_0
  N21: IC1.pin4, R10.Pin_0
  N22: IC1.pin5, R11.Pin_0
  N23: IC1.pin13, J2.pin5
  N24: IC1.pin14, J2.pin4
  N25: IC1.pin15, J2.pin3
  N26: IC1.pin16, J2.pin2
  N27: J1.pin4, J3.pin1, R3.Pin_1
  N28: J1.pin5, R4.Pin_1, J4.pin1
  N29: J1.pin6, R5.Pin_1, J5.pin1
  N30: J1.pin7, R6.Pin_1, J6.pin1
